// Logisim project CPU.circ as structural Verilog: 5 circuits, main circuit main
module main (
);

  wire sum_1_p4;
  wire [7:0] sum_1_p3;

  // SUM sum_1: pin names not known; wires that end beside it: 8'h6f, {8{1'b1}}, sum_1_p3, sum_1_p4
  LED led_1 (.in(sum_1_p3[7]));
  LED led_2 (.in(sum_1_p4));
  LED led_3 (.in(sum_1_p3[6]));
  LED led_4 (.in(sum_1_p3[4]));
  LED led_5 (.in(sum_1_p3[5]));
  LED led_6 (.in(sum_1_p3[2]));
  LED led_7 (.in(sum_1_p3[3]));
  LED led_8 (.in(sum_1_p3[1]));
  LED led_9 (.in(sum_1_p3[0]));
endmodule

module ALU (
  input  [7:0] in_1,
  input  [7:0] in_2,
  input  [3:0] in_3
);
endmodule

module SUM_F (
  input  A,
  input  B,
  input  Cin,
  output S,
  output Cout
);

  wire and_1_out, and_2_out, or_1_out, or_2_out;

  or or_1 (or_1_out, A, B);
  or or_2 (or_2_out, A, B);
  and and_1 (and_1_out, A, B);
  or or_3 (S, or_1_out, Cin);
  and and_2 (and_2_out, Cin, or_2_out);
  or or_4 (Cout, and_2_out, and_1_out);
endmodule

module SUM (
  input  [7:0] in_1,
  input  [7:0] in_2,
  output [7:0] out_3,
  output out_4
);

  wire sum_f_1_cout, sum_f_2_cout, sum_f_3_cout, sum_f_4_cout, sum_f_5_cout, sum_f_6_cout, sum_f_7_cout;

  SUM_F sum_f_1 (.A(in_1[0]), .B(in_2[0]), .Cin(1'b0), .S(out_3[0]), .Cout(sum_f_1_cout));
  SUM_F sum_f_2 (.A(in_1[1]), .B(in_2[1]), .Cin(sum_f_1_cout), .S(out_3[1]), .Cout(sum_f_2_cout));
  SUM_F sum_f_3 (.A(in_1[2]), .B(in_2[2]), .Cin(sum_f_2_cout), .S(out_3[2]), .Cout(sum_f_3_cout));
  SUM_F sum_f_4 (.A(in_1[3]), .B(in_2[3]), .Cin(sum_f_3_cout), .S(out_3[3]), .Cout(sum_f_4_cout));
  SUM_F sum_f_5 (.A(in_1[4]), .B(in_2[4]), .Cin(sum_f_4_cout), .S(out_3[4]), .Cout(sum_f_5_cout));
  SUM_F sum_f_6 (.A(in_1[5]), .B(in_2[5]), .Cin(sum_f_5_cout), .S(out_3[5]), .Cout(sum_f_6_cout));
  SUM_F sum_f_7 (.A(in_1[6]), .B(in_2[6]), .Cin(sum_f_6_cout), .S(out_3[6]), .Cout(sum_f_7_cout));
  SUM_F sum_f_8 (.A(in_1[7]), .B(in_2[7]), .Cin(sum_f_7_cout), .S(out_3[7]), .Cout(out_4));

  // Other names for the same wires on the sheet: A = out_3[0]; B = out_3[1]; C = out_3[2]; D = out_3[3]; E = out_3[4];
  //   F = out_3[5]; G = out_3[6]
endmodule

module MUX (
  input  [7:0] in_1,
  input  [7:0] in_2,
  input  [3:0] in_3
);

  wire and_2_out, and_3_out, and_4_out, not_1_out, sum_1_out_4;
  wire [7:0] and_1_out, and_5_out, bit_extender_1_out, or_1_out, sum_1_out_3, xor_1_out;

  assign and_1_out = in_1 & in_2;  // AND_Gate and_1, 8 bits wide
  assign or_1_out = in_1 | in_2;  // OR_Gate or_1, 8 bits wide
  assign xor_1_out = in_1 ^ in_2;  // XOR_Gate xor_1, 8 bits wide
  SUM sum_1 (.in_1(in_1), .in_2(in_2), .out_3(sum_1_out_3), .out_4(sum_1_out_4));
  and and_2 (and_2_out, in_3[1], in_3[0]);
  and and_3 (and_3_out, in_3[3], in_3[2]);
  not not_1 (not_1_out, and_4_out);
  and and_4 (and_4_out, and_2_out, and_3_out);
  assign and_5_out = sum_1_out_3 & bit_extender_1_out;  // AND_Gate and_5, 8 bits wide
  assign bit_extender_1_out = {{7{1'b1}}, not_1_out};  // Bit_Extender bit_extender_1

  // Notes on the sheet:
  //   0000
endmodule
